// Logisim project ex5.circ as structural Verilog: 5 circuits, main circuit rotr
module rotr (
  input  [15:0] A,
  input  [3:0] B,
  output [15:0] Out1
);

  wire [3:0] adder_1_out, adder_2_out, negator_1_out;
  wire [15:0] shifter_1_out, shifter_2_out;

  Negator #(.width(4)) negator_1 (.in(B), .out(negator_1_out));
  Adder #(.width(4)) adder_1 (.a(negator_1_out), .b(4'b1111), .out(adder_1_out));  // open: cin, cout
  Shifter #(.width(16)) shifter_1 (.in(A), .\dist (adder_2_out), .out(shifter_1_out));
  Shifter #(.width(16), .shift("lr")) shifter_2 (.in(A), .\dist (B), .out(shifter_2_out));
  Adder #(.width(4)) adder_2 (.a(adder_1_out), .b(4'b0001), .out(adder_2_out));  // open: cin, cout
  assign Out1 = shifter_1_out | shifter_2_out;  // OR_Gate or_1, 16 bits wide

  // Notes on the sheet:
  //   PUT CIRCUITRY HERE
endmodule

module rot8 (
  input  [15:0] in_1,
  output [15:0] out_2
);


  // Notes on the sheet:
  //   PUT CIRCUITRY HERE
endmodule

module rot4 (
  input  [15:0] in_1,
  output [15:0] out_2
);


  // Notes on the sheet:
  //   PUT CIRCUITRY HERE
endmodule

module rot2 (
  input  [15:0] in_1,
  output [15:0] out_2
);


  // Notes on the sheet:
  //   PUT CIRCUITRY HERE
endmodule

module rot1 (
  input  [15:0] in_1,
  output [15:0] out_2
);


  // Notes on the sheet:
  //   PUT CIRCUITRY HERE
endmodule
